# Fritzing sketch LCD SCREEN (saved by Fritzing 0.9.3b)
breadboards: 1

parts:
  R1 = Resistor [tolerance=±20% resistance=10k package=THT]
  R2 = Rotary Potentiometer (Large) [maximum_resistance=10kΩ package=THT]
  part = LCD-16X2 [package=lcd-8x2-kit]

nets:
  N1: R1.Pin_0, part.R_W
  GND: R1.Pin_1, R2.leg2, part.VSS, part.K
  N2: R2.wiper, part.VO
  5V: part.VDD, part.A
